// Logisim project TP1_Unidade Controladora.circ as structural Verilog: 18 circuits, main circuit Memoria
module main (
  output [7:0] out_1,
  output out_2
);

  wire and_1_out, and_2_out, comparator_1_eq, comparator_2_eq, d_ff_1_q, data_addr, flag_1_out_6,
       flag_1_out_7, flag_1_out_8, flag_1_out_9, in_out, io_e, io_s, or_1_out, register_2_q,
       uc_editada_1_flags_set, uc_editada_1_init, uc_editada_1_ir_set, uc_editada_1_to_acc_enable,
       uc_editada_1_to_acc_set, uc_editada_1_to_bus1, uc_editada_1_to_iar_enable, uc_editada_1_to_iar_set,
       uc_editada_1_to_mar_set, uc_editada_1_to_r0_enable, uc_editada_1_to_r0_set, uc_editada_1_to_r1_enable,
       uc_editada_1_to_r1_set, uc_editada_1_to_r2_enable, uc_editada_1_to_r2_set, uc_editada_1_to_r3_enable,
       uc_editada_1_to_r3_set, uc_editada_1_to_ram_enable, uc_editada_1_to_ram_set, uc_editada_1_to_tmp_set,
       ula_1_a_igual_b, ula_1_a_maior, ula_1_carry_out, ula_1_zero;
  wire [2:0] uc_editada_1_ula_op;
  wire [6:0] bit_extender_2_out, keyboard_1_data;
  wire [7:0] acumulador_q, bit_extender_1_out, bus_1_1_out_3, controlled_buffer_1_out, IAR_q, IR_q, MAR_q,
       R0_q, R1_q, R2_q, R3_q, register_3_q, temp_q, ula_1_out_5;

  Register temp (.D(controlled_buffer_1_out), .Q(temp_q), .clk(uc_editada_1_to_tmp_set));  // open: en, clr
  Bus_1 bus_1_1 (.in_1(temp_q), .out_3(bus_1_1_out_3), .in_2(uc_editada_1_to_bus1));
  ULA ula_1 (
    .A(controlled_buffer_1_out), .B(bus_1_1_out_3), .out_5(ula_1_out_5), .seletor(uc_editada_1_ula_op),
    .carry_out(ula_1_carry_out), .A_maior(ula_1_a_maior), .A_igual_B(ula_1_a_igual_b), .zero(ula_1_zero));
  Register acumulador (.D(ula_1_out_5), .Q(acumulador_q), .clk(uc_editada_1_to_acc_set));  // open: en, clr
  Comparator comparator_1 (.a(controlled_buffer_1_out), .b(8'h97), .eq(comparator_1_eq));  // open: gt, lt
  Comparator comparator_2 (.a(controlled_buffer_1_out), .b(8'h98), .eq(comparator_2_eq));  // open: gt, lt
  flag flag_1 (
    .in_1(ula_1_carry_out), .in_2(ula_1_a_maior), .in_3(ula_1_a_igual_b), .in_5(ula_1_zero),
    .in_4(uc_editada_1_flags_set), .out_6(flag_1_out_6), .out_7(flag_1_out_7), .out_8(flag_1_out_8),
    .out_9(flag_1_out_9));
  assign controlled_buffer_1_out = uc_editada_1_to_acc_enable ? acumulador_q : 8'bz;  // Controlled_Buffer controlled_buffer_1
  D_Flip_Flop d_ff_1 (.clk(io_e), .D(register_2_q), .Q(d_ff_1_q));  // open: Qn, preset, reset
  and and_1 (and_1_out, io_s, data_addr, in_out);
  Register #(.width(1)) register_1 (.D(comparator_2_eq), .Q(out_2), .clk(and_2_out));  // open: en, clr
  and and_2 (and_2_out, io_s, data_addr, in_out);
  Keyboard keyboard_1 (.clk(d_ff_1_q), .re(register_2_q), .data(keyboard_1_data));  // open: clr, avail
  Register #(.width(1)) register_2 (.D(comparator_1_eq), .Q(register_2_q), .clk(and_1_out));  // open: en, clr
  assign controlled_buffer_1_out = uc_editada_1_to_r0_enable ? R0_q : 8'bz;  // Controlled_Buffer controlled_buffer_2
  Register R0 (.D(controlled_buffer_1_out), .Q(R0_q), .clk(uc_editada_1_to_r0_set));  // open: en, clr
  assign bit_extender_1_out = {{1{1'b0}}, keyboard_1_data};  // Bit_Extender bit_extender_1
  Bit_Extender #(.out_width(7), .\type ("zero")) bit_extender_2 (
    .in(controlled_buffer_1_out), .out(bit_extender_2_out));
  Register IAR (.D(controlled_buffer_1_out), .Q(IAR_q), .clk(uc_editada_1_to_iar_set));  // open: en, clr
  assign controlled_buffer_1_out = uc_editada_1_to_iar_enable ? IAR_q : 8'bz;  // Controlled_Buffer controlled_buffer_3
  assign controlled_buffer_1_out = io_e ? register_3_q : 8'bz;  // Controlled_Buffer controlled_buffer_4
  Register register_3 (.D(bit_extender_1_out), .Q(register_3_q), .clk(d_ff_1_q));  // open: en, clr
  TTY tty_1 (.data(bit_extender_2_out), .clk(io_s), .we(out_2), .clr(out_2));
  assign controlled_buffer_1_out = uc_editada_1_to_r1_enable ? R1_q : 8'bz;  // Controlled_Buffer controlled_buffer_5
  Register R1 (.D(controlled_buffer_1_out), .Q(R1_q), .clk(uc_editada_1_to_r1_set));  // open: en, clr
  Register IR (.D(controlled_buffer_1_out), .Q(IR_q), .clk(uc_editada_1_ir_set));  // open: en, clr
  UC_editada uc_editada_1 (
    .ULA_op(uc_editada_1_ula_op), .from_cout(flag_1_out_6), .from_larger(flag_1_out_7),
    .from_equal(flag_1_out_8), .from_zero(flag_1_out_9), .flags_set(uc_editada_1_flags_set),
    .to_bus1(uc_editada_1_to_bus1), .to_TMP_set(uc_editada_1_to_tmp_set), .to_R0_set(uc_editada_1_to_r0_set),
    .to_R0_enable(uc_editada_1_to_r0_enable), .to_R1_set(uc_editada_1_to_r1_set),
    .to_R1_enable(uc_editada_1_to_r1_enable), .to_R2_set(uc_editada_1_to_r2_set),
    .to_R2_enable(uc_editada_1_to_r2_enable), .to_R3_set(uc_editada_1_to_r3_set),
    .to_R3_enable(uc_editada_1_to_r3_enable), .to_MAR_set(uc_editada_1_to_mar_set),
    .to_ACC_set(uc_editada_1_to_acc_set), .to_ACC_enable(uc_editada_1_to_acc_enable),
    .to_IAR_set(uc_editada_1_to_iar_set), .to_IAR_enable(uc_editada_1_to_iar_enable), .IR_input(IR_q),
    .IR_set(uc_editada_1_ir_set), .input_output(in_out), .Data_address(data_addr), .to_IO_enable(io_e),
    .to_IO_set(io_s), .to_RAM_set(uc_editada_1_to_ram_set), .to_RAM_enable(uc_editada_1_to_ram_enable),
    .init(uc_editada_1_init));
  assign controlled_buffer_1_out = uc_editada_1_to_r2_enable ? R2_q : 8'bz;  // Controlled_Buffer controlled_buffer_6
  Register R2 (.D(controlled_buffer_1_out), .Q(R2_q), .clk(uc_editada_1_to_r2_set));  // open: en, clr
  assign controlled_buffer_1_out = uc_editada_1_to_r3_enable ? R3_q : 8'bz;  // Controlled_Buffer controlled_buffer_7
  Register R3 (.D(controlled_buffer_1_out), .Q(R3_q), .clk(uc_editada_1_to_r3_set));  // open: en, clr
  LED led_1 (.in(uc_editada_1_init));
  Register MAR (.D(controlled_buffer_1_out), .Q(MAR_q), .clk(uc_editada_1_to_mar_set));  // open: en, clr
  or or_1 (or_1_out, uc_editada_1_to_ram_set, uc_editada_1_to_ram_enable);
  RAM #(.\type ("nonvolatile")) ram_1 (
    .addr(MAR_q), .we(uc_editada_1_to_ram_set), .oe(uc_editada_1_to_ram_enable), .clk(or_1_out),
    .din(controlled_buffer_1_out), .dout(out_1));
  assign controlled_buffer_1_out = uc_editada_1_to_ram_enable ? out_1 : 8'bz;  // Controlled_Buffer controlled_buffer_8

  // Notes on the sheet:
  //   Teclado
  //   monitor
  //   0b1001 0111 ->  0x97
  //   0b1001 1111 ->  0x98
endmodule

// M
module Memoria (
  input  i,
  input  s,
  output o
);

  wire nand_1_out, nand_2_out, nand_4_out;

  nand nand_1 (nand_1_out, i, s);
  not nand_2 (nand_2_out, s);  // NAND_Gate
  nand nand_3 (o, nand_1_out, nand_4_out);
  nand nand_4 (nand_4_out, o, nand_2_out);
endmodule

module B (
  input  i0,
  input  i1,
  input  i2,
  input  i3,
  input  i4,
  input  i5,
  input  i6,
  input  i7,
  input  s,
  output o0,
  output o1,
  output o2,
  output o3,
  output o4,
  output o5,
  output o6,
  output o7
);

  Memoria memoria_1 (.i(i0), .s(s), .o(o0));
  Memoria memoria_2 (.i(i1), .s(s), .o(o1));
  Memoria memoria_3 (.i(i2), .s(s), .o(o2));
  Memoria memoria_4 (.i(i3), .s(s), .o(o3));
  Memoria memoria_5 (.i(i4), .s(s), .o(o4));
  Memoria memoria_6 (.i(i5), .s(s), .o(o5));
  Memoria memoria_7 (.i(i6), .s(s), .o(o6));
  Memoria memoria_8 (.i(i7), .s(s), .o(o7));
endmodule

module E (
  input  in_1,
  input  in_2,
  input  in_3,
  input  in_4,
  input  in_5,
  input  in_6,
  input  in_7,
  input  in_8,
  input  in_9,
  output out_10,
  output out_11,
  output out_12,
  output out_13,
  output out_14,
  output out_15,
  output out_16,
  output out_17
);

  and and_1 (out_10, in_1, in_9);
  and and_2 (out_11, in_2, in_9);
  and and_3 (out_12, in_3, in_9);
  and and_4 (out_13, in_4, in_9);
  and and_5 (out_14, in_5, in_9);
  and and_6 (out_15, in_6, in_9);
  and and_7 (out_16, in_7, in_9);
  and and_8 (out_17, in_8, in_9);
endmodule

module Registrador (
  input  [7:0] in_1,
  input  s,
  input  enable,
  output [7:0] out_4
);

  wire b_1_o0, b_1_o1, b_1_o2, b_1_o3, b_1_o4, b_1_o5, b_1_o6, b_1_o7;

  B b_1 (
    .i0(in_1[0]), .i1(in_1[1]), .i2(in_1[2]), .i3(in_1[3]), .i4(in_1[4]), .i5(in_1[5]), .i6(in_1[6]),
    .i7(in_1[7]), .s(s), .o0(b_1_o0), .o1(b_1_o1), .o2(b_1_o2), .o3(b_1_o3), .o4(b_1_o4), .o5(b_1_o5),
    .o6(b_1_o6), .o7(b_1_o7));
  E e_1 (
    .in_1(b_1_o0), .in_2(b_1_o1), .in_3(b_1_o2), .in_4(b_1_o3), .in_5(b_1_o4), .in_6(b_1_o5), .in_7(b_1_o6),
    .in_8(b_1_o7), .in_9(enable), .out_10(out_4[0]), .out_11(out_4[1]), .out_12(out_4[2]), .out_13(out_4[3]),
    .out_14(out_4[4]), .out_15(out_4[5]), .out_16(out_4[6]), .out_17(out_4[7]));
endmodule

module dec_3x8 (
  input  a,
  input  b,
  input  c,
  output s0,
  output s1,
  output s2,
  output s3,
  output s4,
  output s5,
  output s6,
  output s7
);

  wire not_1_out, not_2_out, not_3_out;

  not not_1 (not_1_out, c);
  not not_2 (not_2_out, b);
  not not_3 (not_3_out, a);
  and and_1 (s0, not_3_out, not_2_out, not_1_out);
  and and_2 (s1, not_3_out, not_2_out, c);
  and and_3 (s2, not_3_out, b, not_1_out);
  and and_4 (s3, not_3_out, b, c);
  and and_5 (s4, a, not_2_out, not_1_out);
  and and_6 (s5, a, not_2_out, c);
  and and_7 (s6, a, b, not_1_out);
  and and_8 (s7, a, b, c);
endmodule

module dec_4x16 (
  input  in_1,
  input  in_2,
  input  in_3,
  input  in_4,
  output [15:0] out_5
);

  Decoder #(.enable("false"), .select(4)) decoder_1 (
    .out0(out_5[0]), .out1(out_5[1]), .out2(out_5[2]), .out3(out_5[3]), .out4(out_5[4]), .out5(out_5[5]),
    .out6(out_5[6]), .out7(out_5[7]), .out8(out_5[8]), .out9(out_5[9]), .out10(out_5[10]), .out11(out_5[11]),
    .out12(out_5[12]), .out13(out_5[13]), .out14(out_5[14]), .out15(out_5[15]), .sel({in_4, in_3, in_2, in_1}));
endmodule

module Memoria_16x16 (
  input  [7:0] in_1,
  input  e,
  input  [7:0] in_3,
  input  seletor,
  input  enable,
  output [7:0] out_6
);

  wire and_1_out, and_2_out, and_3_out, decoder_1_out0, decoder_1_out1, decoder_1_out2, decoder_1_out3,
       decoder_1_out4, decoder_1_out5, decoder_1_out6, decoder_1_out7, decoder_1_out8, decoder_1_out9,
       decoder_1_out10, decoder_1_out11, decoder_1_out12, decoder_1_out13, decoder_1_out14, decoder_1_out15,
       decoder_2_out0, decoder_2_out1, decoder_2_out2, decoder_2_out3, decoder_2_out4, decoder_2_out5,
       decoder_2_out6, decoder_2_out7, decoder_2_out8, decoder_2_out9, decoder_2_out10, decoder_2_out11,
       decoder_2_out12, decoder_2_out13, decoder_2_out14, decoder_2_out15;
  wire [3:0] b_1_o0, b_1_o4;

  B b_1 (
    .i0(in_1[0]), .i1(in_1[1]), .i2(in_1[2]), .i3(in_1[3]), .i4(in_1[4]), .i5(in_1[5]), .i6(in_1[6]),
    .i7(in_1[7]), .s(e), .o0(b_1_o0[0]), .o1(b_1_o0[1]), .o2(b_1_o0[2]), .o3(b_1_o0[3]), .o4(b_1_o4[0]),
    .o5(b_1_o4[1]), .o6(b_1_o4[2]), .o7(b_1_o4[3]));
  Decoder #(.enable("false"), .select(4)) decoder_1 (
    .out0(decoder_1_out0), .out1(decoder_1_out1), .out2(decoder_1_out2), .out3(decoder_1_out3),
    .out4(decoder_1_out4), .out5(decoder_1_out5), .out6(decoder_1_out6), .out7(decoder_1_out7),
    .out8(decoder_1_out8), .out9(decoder_1_out9), .out10(decoder_1_out10), .out11(decoder_1_out11),
    .out12(decoder_1_out12), .out13(decoder_1_out13), .out14(decoder_1_out14), .out15(decoder_1_out15),
    .sel(b_1_o4));
  Decoder #(.enable("false"), .select(4)) decoder_2 (
    .out0(decoder_2_out0), .out1(decoder_2_out1), .out2(decoder_2_out2), .out3(decoder_2_out3),
    .out4(decoder_2_out4), .out5(decoder_2_out5), .out6(decoder_2_out6), .out7(decoder_2_out7),
    .out8(decoder_2_out8), .out9(decoder_2_out9), .out10(decoder_2_out10), .out11(decoder_2_out11),
    .out12(decoder_2_out12), .out13(decoder_2_out13), .out14(decoder_2_out14), .out15(decoder_2_out15),
    .sel(b_1_o0));
  and and_1 (and_1_out, decoder_1_out0, decoder_2_out0);
  and and_2 (and_2_out, and_1_out, seletor);
  and and_3 (and_3_out, and_1_out, enable);
  Registrador registrador_1 (.in_1(in_3), .s(and_2_out), .enable(and_3_out), .out_4(out_6));
endmodule

module memoria_256 (
  input  [7:0] endereco,
  input  escrita,
  input  saida,
  input  [7:0] in_4,
  input  clock,
  output [7:0] out_6
);

  RAM ram_1 (.addr(endereco), .we(escrita), .oe(saida), .clk(clock), .din(in_4), .dout(out_6));
endmodule

// R
module SHR (
  input  c_in,
  input  [7:0] entrada,
  output [7:0] saida,
  output c_out
);


  assign c_out = entrada[0];
  assign saida = {c_in, entrada[7:1]};
endmodule

// L
module SHL (
  input  c_in,
  input  [7:0] entrada,
  output [7:0] saida,
  output c_out
);


  assign c_out = entrada[7];
  assign saida = {entrada[6:0], c_in};
endmodule

module S (
  input  [7:0] in_1,
  input  [7:0] in_2,
  output SHL,
  output [7:0] out_4,
  output SHR,
  output [7:0] out_6,
  output out_7
);

  wire shl_1_c_out;

  SHL shl_1 (.entrada(in_1), .c_in(SHL), .c_out(shl_1_c_out), .saida(out_4));
  SHR shr_1 (.entrada(in_2), .c_in(SHR), .c_out(out_7), .saida(out_6));
endmodule

module ULA (
  input  [2:0] seletor,
  input  [7:0] A,
  input  [7:0] B,
  output carry_out,
  output [7:0] out_5,
  output A_maior,
  output A_igual_B,
  output zero
);

  wire adder_1_cout, or_2_out, shl_1_c_out, shr_1_c_out;
  wire [7:0] adder_1_out, and_1_out, not_1_out, or_1_out, shl_1_saida, shr_1_saida, xor_1_out;

  Adder adder_1 (.a(A), .b(B), .out(adder_1_out), .cin(1'b0), .cout(adder_1_cout));
  SHR shr_1 (.entrada(A), .c_in(1'b0), .c_out(shr_1_c_out), .saida(shr_1_saida));
  SHL shl_1 (.entrada(A), .c_in(1'b0), .c_out(shl_1_c_out), .saida(shl_1_saida));
  assign not_1_out = ~A;  // NOT_Gate not_1, 8 bits wide
  assign and_1_out = A & B;  // AND_Gate and_1, 8 bits wide
  assign or_1_out = A | B;  // OR_Gate or_1, 8 bits wide
  assign xor_1_out = A ^ B;  // XOR_Gate xor_1, 8 bits wide
  Comparator comparator_1 (.a(A), .b(B), .gt(A_maior), .eq(A_igual_B));  // open: lt
  Multiplexer #(.select(3), .width(8)) multiplexer_1 (
    .in0(adder_1_out), .in1(shr_1_saida), .in2(shl_1_saida), .in3(not_1_out), .in4(and_1_out),
    .in5(or_1_out), .in6(xor_1_out), .in7(A), .out(out_5), .sel(seletor));
  Multiplexer #(.select(3)) multiplexer_2 (
    .in0(adder_1_cout), .in1(shr_1_c_out), .in2(shl_1_c_out), .in3(1'b0), .in4(1'b0), .in5(1'b0), .in6(1'b0),
    .in7(1'b0), .out(carry_out), .sel(seletor));
  or or_2 (or_2_out, out_5[0], out_5[1], out_5[2], out_5[3], out_5[4], out_5[5], out_5[6], out_5[7]);
  not not_2 (zero, or_2_out);
endmodule

module clk (
  output clk_s,
  output out_2,
  output clK_e
);

  wire clock_d_out;

  Clock #(.highDuration(2), .lowDuration(2)) clock_normal (.out(out_2));
  Clock #(.highDuration(2), .lowDuration(2), .phaseOffset(3)) clock_d (.out(clock_d_out));
  and and_1 (clk_s, clock_d_out, out_2);
  or or_1 (clK_e, out_2, clock_d_out);

  // Notes on the sheet:
  //   clock_e(nable)--> porta OR
  //   clock_s(et)--> porta AND
endmodule

module stepper (
  input  in_1,
  output out_2,
  output out_3,
  output out_4,
  output out_5,
  output out_6,
  output out_7,
  output out_8
);

  wire decoder_1_out7;
  wire [2:0] counter_1_q;

  Counter #(.max('h7), .width(3)) counter_1 (
    .D(counter_1_q), .Q(counter_1_q), .clk(in_1), .clr(decoder_1_out7));  // open: load, count, carry, up
  Decoder #(.enable("false"), .select(3)) decoder_1 (
    .out0(out_2), .out1(out_3), .out2(out_4), .out3(out_5), .out4(out_6), .out5(out_7), .out6(out_8),
    .out7(decoder_1_out7), .sel(counter_1_q));
endmodule

// b1
module Bus_1 (
  input  [7:0] in_1,
  input  in_2,
  output [7:0] out_3
);

  Multiplexer #(.width(8)) multiplexer_1 (.in0(in_1), .in1(8'h1), .out(out_3), .sel(in_2));
endmodule

module flag (
  input  in_1,
  input  in_2,
  input  in_3,
  input  in_4,
  input  in_5,
  output out_6,
  output out_7,
  output out_8,
  output out_9
);

  Register #(.width(4)) register_1 (
    .D({in_5, in_3, in_2, in_1}), .Q({out_9, out_8, out_7, out_6}), .clk(in_4));  // open: en, clr
endmodule

module UC_editada (
  input  from_cout,
  input  from_larger,
  input  from_equal,
  input  from_zero,
  input  [7:0] IR_input,
  output to_bus1,
  output to_TMP_set,
  output to_R0_set,
  output to_R0_enable,
  output to_R1_set,
  output to_R1_enable,
  output to_R2_set,
  output to_R2_enable,
  output to_R3_set,
  output to_R3_enable,
  output to_MAR_set,
  output to_RAM_set,
  output [2:0] ULA_op,
  output to_RAM_enable,
  output init,
  output flags_set,
  output to_IAR_set,
  output to_IAR_enable,
  output IR_set,
  output input_output,
  output Data_address,
  output to_IO_enable,
  output to_IO_set,
  output to_ACC_set,
  output to_ACC_enable
);

  wire A_out, and_5_out, and_6_out, and_7_out, and_8_out, and_9_out, and_10_out, and_11_out, and_12_out,
       and_16_out, and_17_out, and_18_out, and_19_out, and_20_out, and_21_out, and_22_out, and_23_out,
       and_24_out, and_25_out, and_26_out, and_27_out, and_28_out, and_29_out, and_30_out, and_31_out,
       and_32_out, and_33_out, and_34_out, and_35_out, and_36_out, and_37_out, and_38_out, and_39_out,
       and_40_out, and_41_out, and_42_out, and_43_out, C_out, clk_1_out_2, clk_e, clk_s, decoder_1_out0,
       decoder_1_out1, decoder_1_out2, decoder_1_out3, decoder_2_out0, decoder_2_out1, decoder_2_out2,
       decoder_2_out3, decoder_3_out0, decoder_3_out1, decoder_3_out2, decoder_3_out3, decoder_3_out4,
       decoder_3_out5, decoder_3_out6, decoder_3_out7, decoder_4_out0, decoder_4_out1, decoder_4_out2,
       decoder_4_out3, E_out, flags_s, not_1_out, not_2_out, not_3_out, or_6_out, or_7_out, or_8_out,
       or_9_out, or_10_out, or_11_out, or_12_out, or_13_out, or_14_out, or_15_out, or_16_out, S1, S2, S3, S4,
       S5, S6, Z_out;

  clk clk_1 (.clk_s(clk_s), .out_2(clk_1_out_2), .clK_e(clk_e));
  or or_1 (to_R0_enable, and_5_out, and_9_out);
  or or_2 (to_R1_enable, and_6_out, and_10_out);
  or or_3 (to_R2_enable, and_7_out, and_11_out);
  or or_4 (to_R3_enable, and_8_out, and_12_out);
  and and_1 (to_IAR_enable, clk_e, or_6_out);
  and and_2 (to_RAM_enable, clk_e, or_7_out);
  and and_3 (to_ACC_enable, clk_e, or_8_out);
  and and_4 (to_IO_enable, clk_e, and_39_out);
  and and_5 (and_5_out, clk_e, or_9_out, decoder_1_out0);
  and and_6 (and_6_out, clk_e, or_9_out, decoder_1_out1);
  and and_7 (and_7_out, clk_e, or_9_out, decoder_1_out2);
  and and_8 (and_8_out, clk_e, or_9_out, decoder_1_out3);
  and and_9 (and_9_out, clk_e, or_10_out, decoder_2_out0);
  and and_10 (and_10_out, clk_e, or_10_out, decoder_2_out1);
  and and_11 (and_11_out, clk_e, or_10_out, decoder_2_out2);
  and and_12 (and_12_out, clk_e, or_10_out, decoder_2_out3);
  or or_5 (to_bus1, S1, and_31_out, and_30_out, and_27_out);
  or or_6 (or_6_out, S1, and_27_out, and_29_out, and_30_out);
  or or_7 (or_7_out, S2, and_43_out, and_37_out, and_36_out, and_34_out);
  or or_8 (or_8_out, S3, and_38_out, and_42_out, and_41_out);
  or or_9 (or_9_out, and_24_out, and_35_out, and_28_out, and_32_out);
  or or_10 (or_10_out, and_26_out, and_25_out, and_33_out);
  and and_13 (ULA_op[0], S5, IR_input[7], IR_input[4]);
  and and_14 (ULA_op[1], S5, IR_input[7], IR_input[5]);
  and and_15 (ULA_op[2], S5, IR_input[7], IR_input[6]);
  Decoder #(.enable("false"), .select(2)) decoder_1 (
    .out0(decoder_1_out0), .out1(decoder_1_out1), .out2(decoder_1_out2), .out3(decoder_1_out3),
    .sel(IR_input[1:0]));
  Decoder #(.enable("false"), .select(2)) decoder_2 (
    .out0(decoder_2_out0), .out1(decoder_2_out1), .out2(decoder_2_out2), .out3(decoder_2_out3),
    .sel(IR_input[3:2]));
  not not_1 (not_1_out, IR_input[7]);
  Decoder #(.enable("false"), .select(3)) decoder_3 (
    .out0(decoder_3_out0), .out1(decoder_3_out1), .out2(decoder_3_out2), .out3(decoder_3_out3),
    .out4(decoder_3_out4), .out5(decoder_3_out5), .out6(decoder_3_out6), .out7(decoder_3_out7),
    .sel(IR_input[6:4]));
  and and_16 (and_16_out, not_1_out, decoder_3_out0);
  and and_17 (and_17_out, not_1_out, decoder_3_out1);
  and and_18 (and_18_out, not_1_out, decoder_3_out2);
  and and_19 (and_19_out, not_1_out, decoder_3_out3);
  and and_20 (and_20_out, not_1_out, decoder_3_out4);
  and and_21 (and_21_out, not_1_out, decoder_3_out5);
  and and_22 (and_22_out, not_1_out, decoder_3_out6);
  and and_23 (and_23_out, not_1_out, decoder_3_out7);
  and C (C_out, IR_input[3], from_cout);
  and A (A_out, IR_input[2], from_larger);
  and E (E_out, IR_input[1], from_equal);
  and Z (Z_out, IR_input[0], from_zero);
  and and_24 (and_24_out, S4, IR_input[7]);
  and and_25 (and_25_out, S4, and_16_out);
  and and_26 (and_26_out, S4, and_17_out);
  and and_27 (and_27_out, S4, and_18_out);
  and and_28 (and_28_out, S4, and_19_out);
  and and_29 (and_29_out, S4, and_20_out);
  and and_30 (and_30_out, S4, and_21_out);
  and and_31 (and_31_out, S4, and_22_out);
  and and_32 (and_32_out, S4, and_23_out, IR_input[3]);
  not not_2 (not_2_out, IR_input[3]);
  or or_11 (or_11_out, C_out, A_out, E_out, Z_out);
  stepper stepper_1 (
    .in_1(clk_1_out_2), .out_3(S1), .out_4(S2), .out_5(S3), .out_6(S4), .out_7(S5), .out_8(S6), .out_2(init));
  and and_33 (and_33_out, S5, IR_input[7]);
  and and_34 (and_34_out, S5, and_16_out);
  and and_35 (and_35_out, S5, and_17_out);
  and and_36 (and_36_out, S5, and_18_out);
  and and_37 (and_37_out, S5, and_20_out);
  and and_38 (and_38_out, S5, and_21_out);
  and and_39 (and_39_out, S5, and_23_out, not_2_out);
  and and_40 (and_40_out, IR_input[4], IR_input[5], IR_input[6]);
  not not_3 (not_3_out, and_40_out);
  and and_41 (and_41_out, S6, IR_input[7], not_3_out);
  and and_42 (and_42_out, S6, and_18_out);
  and and_43 (and_43_out, S6, and_21_out, or_11_out);
  Decoder #(.enable("false"), .select(2)) decoder_4 (
    .out0(decoder_4_out0), .out1(decoder_4_out1), .out2(decoder_4_out2), .out3(decoder_4_out3),
    .sel(IR_input[1:0]));
  or or_12 (or_12_out, S1, and_27_out, and_30_out, and_25_out, and_26_out, and_29_out);
  or or_13 (or_13_out, S3, and_28_out, and_37_out, and_38_out, and_42_out, and_43_out);
  or or_14 (or_14_out, S1, and_27_out, and_30_out, and_33_out);
  or or_15 (or_15_out, and_31_out, and_33_out);
  or or_16 (or_16_out, and_34_out, and_41_out, and_36_out, and_39_out);
  and and_44 (IR_set, clk_s, S2);
  and and_45 (to_MAR_set, clk_s, or_12_out);
  and and_46 (to_IAR_set, clk_s, or_13_out);
  and and_47 (to_ACC_set, clk_s, or_14_out);
  and and_48 (to_RAM_set, clk_s, and_35_out);
  and and_49 (to_TMP_set, clk_s, and_24_out);
  and and_50 (flags_s, clk_s, or_15_out);
  and and_51 (to_IO_set, clk_s, and_32_out);
  and and_52 (to_R0_set, clk_s, or_16_out, decoder_4_out0);
  and and_53 (to_R1_set, clk_s, or_16_out, decoder_4_out1);
  and and_54 (to_R2_set, clk_s, or_16_out, decoder_4_out2);
  and and_55 (to_R3_set, clk_s, or_16_out, decoder_4_out3);

  assign Data_address = IR_input[2];
  assign input_output = IR_input[3];

  // Other names for the same wires on the sheet: from_IR[7:0] = IR_input; ACC_e = to_ACC_enable; ACC_s = to_ACC_set;
  //   from_large = from_larger; IAR_e = to_IAR_enable; IAR_s = to_IAR_set; IO_e = to_IO_enable; IO_s = to_IO_set;
  //   IR_s = IR_set; MAR_s = to_MAR_set; R0_e = to_R0_enable; R0_s = to_R0_set; R1_e = to_R1_enable; R1_s = to_R1_set;
  //   R2_e = to_R2_enable; R2_s = to_R2_set; R3_e = to_R3_enable; R3_s = to_R3_set; RAM_e = to_RAM_enable;
  //   RAM_s = to_RAM_set; TMP_s = to_TMP_set; to_bus_1 = to_bus1; to_ULA[2:0] = ULA_op
endmodule
