// Logisim project aula 2 Somador de 8 bits.circ as structural Verilog: 3 circuits, main circuit main
module main (
  input  in_1,
  input  [7:0] in_2,
  input  [7:0] in_3,
  output [7:0] out_4,
  output out_5
);

  somador_8bits somador_8bits_1 (.c_in(in_1), .Ent_a(in_2), .Ent_b(in_3), .Saida(out_4), .C_out(out_5));
endmodule

module Somador_1bit (
  input  c_in,
  input  a,
  input  b,
  output saida,
  output c_out
);

  wire and_1_out, and_2_out, and_3_out, xor_1_out;

  xor xor_1 (xor_1_out, a, b);
  and and_1 (and_1_out, a, c_in);
  and and_2 (and_2_out, a, b);
  and and_3 (and_3_out, b, c_in);
  xor xor_2 (saida, xor_1_out, c_in);
  ExactlyOne xor_3 (.out(c_out), .in0(and_1_out), .in1(and_2_out), .in2(and_3_out));
endmodule

module somador_8bits (
  input  c_in,
  input  [7:0] Ent_a,
  input  [7:0] Ent_b,
  output [7:0] Saida,
  output C_out
);

  wire somador_1bit_1_c_out, somador_1bit_2_c_out, somador_1bit_3_c_out, somador_1bit_4_c_out,
       somador_1bit_5_c_out, somador_1bit_6_c_out, somador_1bit_7_c_out;

  Somador_1bit somador_1bit_1 (.a(Ent_a[0]), .b(Ent_b[0]), .c_in(c_in), .saida(Saida[0]), .c_out(somador_1bit_1_c_out));
  Somador_1bit somador_1bit_2 (
    .a(Ent_a[1]), .b(Ent_b[1]), .c_in(somador_1bit_1_c_out), .saida(Saida[1]), .c_out(somador_1bit_2_c_out));
  Somador_1bit somador_1bit_3 (
    .a(Ent_a[2]), .b(Ent_b[2]), .c_in(somador_1bit_2_c_out), .saida(Saida[2]), .c_out(somador_1bit_3_c_out));
  Somador_1bit somador_1bit_4 (
    .a(Ent_a[3]), .b(Ent_b[3]), .c_in(somador_1bit_3_c_out), .saida(Saida[3]), .c_out(somador_1bit_4_c_out));
  Somador_1bit somador_1bit_5 (
    .a(Ent_a[4]), .b(Ent_b[4]), .c_in(somador_1bit_4_c_out), .saida(Saida[4]), .c_out(somador_1bit_5_c_out));
  Somador_1bit somador_1bit_6 (
    .a(Ent_a[5]), .b(Ent_b[5]), .c_in(somador_1bit_5_c_out), .saida(Saida[5]), .c_out(somador_1bit_6_c_out));
  Somador_1bit somador_1bit_7 (
    .a(Ent_a[6]), .b(Ent_b[6]), .c_in(somador_1bit_6_c_out), .saida(Saida[6]), .c_out(somador_1bit_7_c_out));
  Somador_1bit somador_1bit_8 (
    .a(Ent_a[7]), .b(Ent_b[7]), .c_in(somador_1bit_7_c_out), .saida(Saida[7]), .c_out(C_out));
endmodule
