// Logisim project aula 3 Registradores.circ as structural Verilog: 5 circuits, main circuit main
module main (
  input  [7:0] in_1,
  input  s,
  input  in_3,
  input  in_4,
  input  in_5,
  input  e,
  input  in_7,
  input  in_8,
  input  in_9,
  output [7:0] out_10
);

  R r0 (.in_1(in_1), .s(s), .enable(e), .out_4(in_1));
  R r1 (.in_1(in_1), .s(in_3), .enable(in_7), .out_4(in_1));
  R r2 (.in_1(in_1), .s(in_4), .enable(in_8), .out_4(in_1));
  R r3 (.in_1(in_1), .s(in_5), .enable(in_9), .out_4(in_1));

  assign out_10 = in_1;
endmodule

module M (
  input  i,
  input  s,
  output o
);

  wire nand_1_out, nand_2_out, nand_4_out;

  nand nand_1 (nand_1_out, i, s);
  not nand_2 (nand_2_out, s);  // NAND_Gate
  nand nand_3 (o, nand_1_out, nand_4_out);
  nand nand_4 (nand_4_out, o, nand_2_out);
endmodule

module B (
  input  i0,
  input  i1,
  input  i2,
  input  i3,
  input  i4,
  input  i5,
  input  i6,
  input  i7,
  input  s,
  output o0,
  output o1,
  output o2,
  output o3,
  output o4,
  output o5,
  output o6,
  output o7
);

  M m_1 (.i(i0), .s(s), .o(o0));
  M m_2 (.i(i1), .s(s), .o(o1));
  M m_3 (.i(i2), .s(s), .o(o2));
  M m_4 (.i(i3), .s(s), .o(o3));
  M m_5 (.i(i4), .s(s), .o(o4));
  M m_6 (.i(i5), .s(s), .o(o5));
  M m_7 (.i(i6), .s(s), .o(o6));
  M m_8 (.i(i7), .s(s), .o(o7));
endmodule

module E (
  input  in_1,
  input  in_2,
  input  in_3,
  input  in_4,
  input  in_5,
  input  in_6,
  input  in_7,
  input  in_8,
  input  in_9,
  output out_10,
  output out_11,
  output out_12,
  output out_13,
  output out_14,
  output out_15,
  output out_16,
  output out_17
);

  and and_1 (out_10, in_1, in_9);
  and and_2 (out_11, in_2, in_9);
  and and_3 (out_12, in_3, in_9);
  and and_4 (out_13, in_4, in_9);
  and and_5 (out_14, in_5, in_9);
  and and_6 (out_15, in_6, in_9);
  and and_7 (out_16, in_7, in_9);
  and and_8 (out_17, in_8, in_9);
endmodule

module R (
  input  [7:0] in_1,
  input  s,
  input  enable,
  output [7:0] out_4
);

  wire b_1_o0, b_1_o1, b_1_o2, b_1_o3, b_1_o4, b_1_o5, b_1_o6, b_1_o7;

  B b_1 (
    .i0(in_1[0]), .i1(in_1[1]), .i2(in_1[2]), .i3(in_1[3]), .i4(in_1[4]), .i5(in_1[5]), .i6(in_1[6]),
    .i7(in_1[7]), .s(s), .o0(b_1_o0), .o1(b_1_o1), .o2(b_1_o2), .o3(b_1_o3), .o4(b_1_o4), .o5(b_1_o5),
    .o6(b_1_o6), .o7(b_1_o7));
  E e_1 (
    .in_1(b_1_o0), .in_2(b_1_o1), .in_3(b_1_o2), .in_4(b_1_o3), .in_5(b_1_o4), .in_6(b_1_o5), .in_7(b_1_o6),
    .in_8(b_1_o7), .in_9(enable), .out_10(out_4[0]), .out_11(out_4[1]), .out_12(out_4[2]), .out_13(out_4[3]),
    .out_14(out_4[4]), .out_15(out_4[5]), .out_16(out_4[6]), .out_17(out_4[7]));
endmodule
