// Logisim project aula 4 Memória de 256 e MAR.circ as structural Verilog: 9 circuits, main circuit main
module main (
  input  [7:0] in_1,
  input  escrita,
  input  in_3,
  input  saida,
  input  in_5,
  input  set,
  input  in_7,
  input  in_8,
  input  in_9,
  input  enable,
  input  in_11,
  input  in_12,
  input  in_13,
  input  clock,
  input  in_15,
  output [7:0] out_16
);

  wire [7:0] controlled_buffer_1_out, register_1_q, register_2_q, register_3_q, register_4_q, register_5_q;

  assign controlled_buffer_1_out = in_5 ? in_1 : 8'bz;  // Controlled_Buffer controlled_buffer_1
  assign controlled_buffer_1_out = enable ? register_1_q : 8'bz;  // Controlled_Buffer controlled_buffer_2
  Register register_1 (.D(controlled_buffer_1_out), .Q(register_1_q), .clk(set));  // open: en, clr
  assign controlled_buffer_1_out = in_11 ? register_2_q : 8'bz;  // Controlled_Buffer controlled_buffer_3
  Register register_2 (.D(controlled_buffer_1_out), .Q(register_2_q), .clk(in_7));  // open: en, clr
  assign controlled_buffer_1_out = in_12 ? register_3_q : 8'bz;  // Controlled_Buffer controlled_buffer_4
  Register register_3 (.D(controlled_buffer_1_out), .Q(register_3_q), .clk(in_8));  // open: en, clr
  assign controlled_buffer_1_out = in_13 ? register_4_q : 8'bz;  // Controlled_Buffer controlled_buffer_5
  Register register_4 (.D(controlled_buffer_1_out), .Q(register_4_q), .clk(in_9));  // open: en, clr
  Register register_5 (.D(controlled_buffer_1_out), .Q(register_5_q), .clk(in_3));  // open: en, clr
  RAM ram_1 (.addr(register_5_q), .we(escrita), .oe(saida), .clk(clock), .din(controlled_buffer_1_out), .dout(out_16));
  assign controlled_buffer_1_out = in_15 ? out_16 : 8'bz;  // Controlled_Buffer controlled_buffer_6
endmodule

module M (
  input  i,
  input  s,
  output o
);

  wire nand_1_out, nand_2_out, nand_4_out;

  nand nand_1 (nand_1_out, i, s);
  not nand_2 (nand_2_out, s);  // NAND_Gate
  nand nand_3 (o, nand_1_out, nand_4_out);
  nand nand_4 (nand_4_out, o, nand_2_out);
endmodule

module B (
  input  i0,
  input  i1,
  input  i2,
  input  i3,
  input  i4,
  input  i5,
  input  i6,
  input  i7,
  input  s,
  output o0,
  output o1,
  output o2,
  output o3,
  output o4,
  output o5,
  output o6,
  output o7
);

  M m_1 (.i(i0), .s(s), .o(o0));
  M m_2 (.i(i1), .s(s), .o(o1));
  M m_3 (.i(i2), .s(s), .o(o2));
  M m_4 (.i(i3), .s(s), .o(o3));
  M m_5 (.i(i4), .s(s), .o(o4));
  M m_6 (.i(i5), .s(s), .o(o5));
  M m_7 (.i(i6), .s(s), .o(o6));
  M m_8 (.i(i7), .s(s), .o(o7));
endmodule

module E (
  input  in_1,
  input  in_2,
  input  in_3,
  input  in_4,
  input  in_5,
  input  in_6,
  input  in_7,
  input  in_8,
  input  in_9,
  output out_10,
  output out_11,
  output out_12,
  output out_13,
  output out_14,
  output out_15,
  output out_16,
  output out_17
);

  and and_1 (out_10, in_1, in_9);
  and and_2 (out_11, in_2, in_9);
  and and_3 (out_12, in_3, in_9);
  and and_4 (out_13, in_4, in_9);
  and and_5 (out_14, in_5, in_9);
  and and_6 (out_15, in_6, in_9);
  and and_7 (out_16, in_7, in_9);
  and and_8 (out_17, in_8, in_9);
endmodule

module R (
  input  [7:0] in_1,
  input  s,
  input  enable,
  output [7:0] out_4
);

  wire b_1_o0, b_1_o1, b_1_o2, b_1_o3, b_1_o4, b_1_o5, b_1_o6, b_1_o7;

  B b_1 (
    .i0(in_1[0]), .i1(in_1[1]), .i2(in_1[2]), .i3(in_1[3]), .i4(in_1[4]), .i5(in_1[5]), .i6(in_1[6]),
    .i7(in_1[7]), .s(s), .o0(b_1_o0), .o1(b_1_o1), .o2(b_1_o2), .o3(b_1_o3), .o4(b_1_o4), .o5(b_1_o5),
    .o6(b_1_o6), .o7(b_1_o7));
  E e_1 (
    .in_1(b_1_o0), .in_2(b_1_o1), .in_3(b_1_o2), .in_4(b_1_o3), .in_5(b_1_o4), .in_6(b_1_o5), .in_7(b_1_o6),
    .in_8(b_1_o7), .in_9(enable), .out_10(out_4[0]), .out_11(out_4[1]), .out_12(out_4[2]), .out_13(out_4[3]),
    .out_14(out_4[4]), .out_15(out_4[5]), .out_16(out_4[6]), .out_17(out_4[7]));
endmodule

module dec_3x8 (
  input  a,
  input  b,
  input  c,
  output s0,
  output s1,
  output s2,
  output s3,
  output s4,
  output s5,
  output s6,
  output s7
);

  wire not_1_out, not_2_out, not_3_out;

  not not_1 (not_1_out, c);
  not not_2 (not_2_out, b);
  not not_3 (not_3_out, a);
  and and_1 (s0, not_3_out, not_2_out, not_1_out);
  and and_2 (s1, not_3_out, not_2_out, c);
  and and_3 (s2, not_3_out, b, not_1_out);
  and and_4 (s3, not_3_out, b, c);
  and and_5 (s4, a, not_2_out, not_1_out);
  and and_6 (s5, a, not_2_out, c);
  and and_7 (s6, a, b, not_1_out);
  and and_8 (s7, a, b, c);
endmodule

module dec_4x16 (
  input  in_1,
  input  in_2,
  input  in_3,
  input  in_4,
  output [15:0] out_5
);

  Decoder #(.enable("false"), .select(4)) decoder_1 (
    .out0(out_5[0]), .out1(out_5[1]), .out2(out_5[2]), .out3(out_5[3]), .out4(out_5[4]), .out5(out_5[5]),
    .out6(out_5[6]), .out7(out_5[7]), .out8(out_5[8]), .out9(out_5[9]), .out10(out_5[10]), .out11(out_5[11]),
    .out12(out_5[12]), .out13(out_5[13]), .out14(out_5[14]), .out15(out_5[15]), .sel({in_4, in_3, in_2, in_1}));
endmodule

module Memoria_16x16 (
  input  [7:0] in_1,
  input  e,
  input  [7:0] in_3,
  input  seletor,
  input  enable,
  output [7:0] out_6
);

  wire and_1_out, and_2_out, and_3_out, decoder_1_out0, decoder_1_out1, decoder_1_out2, decoder_1_out3,
       decoder_1_out4, decoder_1_out5, decoder_1_out6, decoder_1_out7, decoder_1_out8, decoder_1_out9,
       decoder_1_out10, decoder_1_out11, decoder_1_out12, decoder_1_out13, decoder_1_out14, decoder_1_out15,
       decoder_2_out0, decoder_2_out1, decoder_2_out2, decoder_2_out3, decoder_2_out4, decoder_2_out5,
       decoder_2_out6, decoder_2_out7, decoder_2_out8, decoder_2_out9, decoder_2_out10, decoder_2_out11,
       decoder_2_out12, decoder_2_out13, decoder_2_out14, decoder_2_out15;
  wire [3:0] b_1_o0, b_1_o4;

  B b_1 (
    .i0(in_1[0]), .i1(in_1[1]), .i2(in_1[2]), .i3(in_1[3]), .i4(in_1[4]), .i5(in_1[5]), .i6(in_1[6]),
    .i7(in_1[7]), .s(e), .o0(b_1_o0[0]), .o1(b_1_o0[1]), .o2(b_1_o0[2]), .o3(b_1_o0[3]), .o4(b_1_o4[0]),
    .o5(b_1_o4[1]), .o6(b_1_o4[2]), .o7(b_1_o4[3]));
  Decoder #(.enable("false"), .select(4)) decoder_1 (
    .out0(decoder_1_out0), .out1(decoder_1_out1), .out2(decoder_1_out2), .out3(decoder_1_out3),
    .out4(decoder_1_out4), .out5(decoder_1_out5), .out6(decoder_1_out6), .out7(decoder_1_out7),
    .out8(decoder_1_out8), .out9(decoder_1_out9), .out10(decoder_1_out10), .out11(decoder_1_out11),
    .out12(decoder_1_out12), .out13(decoder_1_out13), .out14(decoder_1_out14), .out15(decoder_1_out15),
    .sel(b_1_o4));
  Decoder #(.enable("false"), .select(4)) decoder_2 (
    .out0(decoder_2_out0), .out1(decoder_2_out1), .out2(decoder_2_out2), .out3(decoder_2_out3),
    .out4(decoder_2_out4), .out5(decoder_2_out5), .out6(decoder_2_out6), .out7(decoder_2_out7),
    .out8(decoder_2_out8), .out9(decoder_2_out9), .out10(decoder_2_out10), .out11(decoder_2_out11),
    .out12(decoder_2_out12), .out13(decoder_2_out13), .out14(decoder_2_out14), .out15(decoder_2_out15),
    .sel(b_1_o0));
  and and_1 (and_1_out, decoder_1_out0, decoder_2_out0);
  and and_2 (and_2_out, and_1_out, seletor);
  and and_3 (and_3_out, and_1_out, enable);
  R r_1 (.in_1(in_3), .s(and_2_out), .enable(and_3_out), .out_4(out_6));
endmodule

module memoria_256 (
  input  [7:0] endereco,
  input  escrita,
  input  saida,
  input  [7:0] in_4,
  input  clock,
  output [7:0] out_6
);

  RAM ram_1 (.addr(endereco), .we(escrita), .oe(saida), .clk(clock), .din(in_4), .dout(out_6));
endmodule
